# Fritzing sketch breadboard_view (saved by Fritzing 0.9.2b)
breadboards: 1

parts:
  R1 = Resistor [tolerance=±5% resistance=220 package=THT]
  J1 = Piezo Speaker
  R4 = Resistor [tolerance=±5% resistance=220 package=THT]
  S1 = Pushbutton [package="[THT]"]
  S2 = Pushbutton [package="[THT]"]
  S3 = Pushbutton [package="[THT]"]
  R5 = Resistor [tolerance=±5% resistance=10k package=THT]
  R6 = Resistor [tolerance=±5% resistance=1M package=THT]
  R7 = Resistor [tolerance=±5% resistance=10k package=THT]
  R8 = Resistor [tolerance=±5% resistance=220 package=THT]
  S4 = Pushbutton [package="[THT]"]
  R2 = Rotary Potentiometer (Small) [maximum_resistance=100kΩ package=THT]
  Part2 = Adafruit NeoPixel Shield [part_number="Adafruit #1430"]
  Part1 = Arduino Uno (Rev3)  # not connected
  U1 = 7-SEGMENT-4DIGIT [package=7-segment-4digit]  # not connected

nets (from the breadboard view):
  N1: R1.Pin_0, R2.leg2
  N2: R1.Pin_1, R4.Pin_1, R5.Pin_0, Part2.GND
  N3: J1.pin1, R4.Pin_0
  N4: J1.pin2, R2.wiper
  N5: S1.Pin_1, S1.Pin_2, S2.Pin_1, S2.Pin_2, S3.Pin_1, S3.Pin_2, R5.Pin_1, S4.Pin_1, S4.Pin_2, Part2.A0
  N6: S1.Pin_3, S1.Pin_4, R6.Pin_1
  N7: S2.Pin_3, S2.Pin_4, R7.Pin_1
  N8: S3.Pin_3, S3.Pin_4, R8.Pin_1
  N9: R6.Pin_0, R7.Pin_0, R8.Pin_0, S4.Pin_3, S4.Pin_4, Part2.ARDUINO_5V
  N10: R2.leg1, Part2.D11

custom parts:
  Adafruit NeoPixel Shield: Put on your sunglasses before putting this shield onto your 'duino - 40 eye-blistering RGB LEDs adorn the NeoPixel shield for a blast of configurable color. Arranged in a 5x8 matrix, each pixel is individually addressable. Only one pin (Digital #6) is required to control all the LEDs. You can cut a trace and use nearly any other pin if you need some customization. To make it easy to start, the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
